// Logisim project projet.circ as structural Verilog
module main (
);

  wire button_1_out, button_2_out, dipswitch_1_sw1, dipswitch_1_sw2, dipswitch_1_sw3, dipswitch_1_sw4,
       dipswitch_1_sw5, dipswitch_1_sw6, dipswitch_1_sw7, dipswitch_1_sw8, dipswitch_1_sw9, dipswitch_1_sw10,
       output_logic_1_a, output_logic_1_b, output_logic_1_c, output_logic_1_d, output_logic_1_e,
       output_logic_1_f, output_logic_1_g, output_logic_1_p, output_logic_2_a, output_logic_2_b,
       output_logic_2_c, output_logic_2_d, output_logic_2_e, output_logic_2_f, output_logic_2_g,
       output_logic_2_p, output_logic_3_a, output_logic_3_b, output_logic_3_c, output_logic_3_d,
       output_logic_3_e, output_logic_3_f, output_logic_3_g, output_logic_3_p, output_logic_4_a,
       output_logic_4_b, output_logic_4_c, output_logic_4_d, output_logic_4_e, output_logic_4_f,
       output_logic_4_g, output_logic_4_p, output_logic_5_a, output_logic_5_b, output_logic_5_c,
       output_logic_5_d, output_logic_5_e, output_logic_5_f, output_logic_5_g, output_logic_5_p,
       output_logic_6_a, output_logic_6_b, output_logic_6_c, output_logic_6_d, output_logic_6_e,
       output_logic_6_f, output_logic_6_g, output_logic_6_p;

  DipSwitch #(.number(10)) dipswitch_1 (
    .sw1(dipswitch_1_sw1), .sw2(dipswitch_1_sw2), .sw3(dipswitch_1_sw3), .sw4(dipswitch_1_sw4),
    .sw5(dipswitch_1_sw5), .sw6(dipswitch_1_sw6), .sw7(dipswitch_1_sw7), .sw8(dipswitch_1_sw8),
    .sw9(dipswitch_1_sw9), .sw10(dipswitch_1_sw10));
  Button button_1 (.out(button_1_out));
  Button button_2 (.out(button_2_out));
  transition_logic transition_logic_1 (
    .B_1(button_1_out), .B_0(button_2_out), .DS_9(dipswitch_1_sw10), .DS_8(dipswitch_1_sw9),
    .DS_7(dipswitch_1_sw8), .DS_6(dipswitch_1_sw7), .DS_5(dipswitch_1_sw6), .DS_4(dipswitch_1_sw5),
    .DS_3(dipswitch_1_sw4), .DS_2(dipswitch_1_sw3), .DS_1(dipswitch_1_sw2), .DS_0(dipswitch_1_sw1));  // open: f
  output_logic output_logic_1 (
    .a(output_logic_1_a), .b(output_logic_1_b), .c(output_logic_1_c), .d(output_logic_1_d),
    .e(output_logic_1_e), .f(output_logic_1_f), .g(output_logic_1_g), .p(output_logic_1_p));  // open: I_5, I_4, I_3, I_2, I_1, I_0
  output_logic output_logic_2 (
    .a(output_logic_2_a), .b(output_logic_2_b), .c(output_logic_2_c), .d(output_logic_2_d),
    .e(output_logic_2_e), .f(output_logic_2_f), .g(output_logic_2_g), .p(output_logic_2_p));  // open: I_5, I_4, I_3, I_2, I_1, I_0
  output_logic output_logic_3 (
    .a(output_logic_3_a), .b(output_logic_3_b), .c(output_logic_3_c), .d(output_logic_3_d),
    .e(output_logic_3_e), .f(output_logic_3_f), .g(output_logic_3_g), .p(output_logic_3_p));  // open: I_5, I_4, I_3, I_2, I_1, I_0
  output_logic output_logic_4 (
    .a(output_logic_4_a), .b(output_logic_4_b), .c(output_logic_4_c), .d(output_logic_4_d),
    .e(output_logic_4_e), .f(output_logic_4_f), .g(output_logic_4_g), .p(output_logic_4_p));  // open: I_5, I_4, I_3, I_2, I_1, I_0
  output_logic output_logic_5 (
    .a(output_logic_5_a), .b(output_logic_5_b), .c(output_logic_5_c), .d(output_logic_5_d),
    .e(output_logic_5_e), .f(output_logic_5_f), .g(output_logic_5_g), .p(output_logic_5_p));  // open: I_5, I_4, I_3, I_2, I_1, I_0
  output_logic output_logic_6 (
    .a(output_logic_6_a), .b(output_logic_6_b), .c(output_logic_6_c), .d(output_logic_6_d),
    .e(output_logic_6_e), .f(output_logic_6_f), .g(output_logic_6_g), .p(output_logic_6_p));  // open: I_5, I_4, I_3, I_2, I_1, I_0
  _7_Segment_Display u_7_segment_display_1 (
    .g(output_logic_1_f), .f(output_logic_1_g), .a(output_logic_1_a), .b(output_logic_1_b),
    .e(output_logic_1_e), .d(output_logic_1_d), .c(output_logic_1_c), .dp(output_logic_1_p));
  _7_Segment_Display u_7_segment_display_2 (
    .g(output_logic_2_f), .f(output_logic_2_g), .a(output_logic_2_a), .b(output_logic_2_b),
    .e(output_logic_2_e), .d(output_logic_2_d), .c(output_logic_2_c), .dp(output_logic_2_p));
  _7_Segment_Display u_7_segment_display_3 (
    .g(output_logic_3_f), .f(output_logic_3_g), .a(output_logic_3_a), .b(output_logic_3_b),
    .e(output_logic_3_e), .d(output_logic_3_d), .c(output_logic_3_c), .dp(output_logic_3_p));
  _7_Segment_Display u_7_segment_display_4 (
    .g(output_logic_4_f), .f(output_logic_4_g), .a(output_logic_4_a), .b(output_logic_4_b),
    .e(output_logic_4_e), .d(output_logic_4_d), .c(output_logic_4_c), .dp(output_logic_4_p));
  _7_Segment_Display u_7_segment_display_5 (
    .g(output_logic_5_f), .f(output_logic_5_g), .a(output_logic_5_a), .b(output_logic_5_b),
    .e(output_logic_5_e), .d(output_logic_5_d), .c(output_logic_5_c), .dp(output_logic_5_p));
  _7_Segment_Display u_7_segment_display_6 (
    .g(output_logic_6_f), .f(output_logic_6_g), .a(output_logic_6_a), .b(output_logic_6_b),
    .e(output_logic_6_e), .d(output_logic_6_d), .c(output_logic_6_c), .dp(output_logic_6_p));
endmodule

module output_logic (
  input  I_5,
  input  I_4,
  input  I_3,
  input  I_2,
  input  I_1,
  input  I_0,
  output a,
  output b,
  output c,
  output d,
  output e,
  output f,
  output g,
  output p
);

  wire and_1_out, and_2_out, and_3_out, and_4_out, and_5_out, and_6_out, and_7_out, and_8_out, and_9_out,
       and_10_out, and_11_out, and_12_out, and_13_out, and_14_out, and_15_out, and_16_out, not_1_out,
       not_2_out, not_3_out, not_4_out, not_5_out, not_6_out, not_7_out, not_8_out, not_9_out, not_10_out,
       not_11_out, not_12_out, not_13_out, not_14_out, not_15_out, not_16_out, not_17_out, not_18_out,
       not_19_out, not_20_out, not_21_out;

  not not_1 (not_1_out, I_2);
  not not_2 (not_2_out, I_0);
  not not_3 (not_3_out, I_1);
  not not_4 (not_4_out, I_0);
  not not_5 (not_5_out, I_1);
  not not_6 (not_6_out, I_2);
  not not_7 (not_7_out, I_0);
  not not_8 (not_8_out, I_2);
  not not_9 (not_9_out, I_0);
  not not_10 (not_10_out, I_1);
  not not_11 (not_11_out, I_2);
  not not_12 (not_12_out, I_0);
  not not_13 (not_13_out, I_0);
  not not_14 (not_14_out, I_1);
  not not_15 (not_15_out, I_0);
  not not_16 (not_16_out, I_1);
  not not_17 (not_17_out, I_0);
  not not_18 (not_18_out, I_2);
  not not_19 (not_19_out, I_1);
  not not_20 (not_20_out, I_0);
  and and_1 (and_1_out, not_1_out, not_2_out);
  and and_2 (and_2_out, I_2, I_0);
  not not_21 (not_21_out, I_2);
  or or_1 (b, not_21_out, and_3_out, and_4_out);
  and and_3 (and_3_out, not_3_out, not_4_out);
  and and_4 (and_4_out, I_1, I_0);
  or or_2 (c, not_5_out, I_0, I_2);
  and and_5 (and_5_out, not_6_out, not_7_out);
  and and_6 (and_6_out, not_8_out, I_1);
  and and_7 (and_7_out, I_1, not_9_out);
  and and_8 (and_8_out, I_2, not_10_out, I_0);
  and and_9 (and_9_out, not_11_out, not_12_out);
  or or_3 (e, and_9_out, and_10_out);
  and and_10 (and_10_out, I_1, not_13_out);
  and and_11 (and_11_out, not_14_out, not_15_out);
  and and_12 (and_12_out, I_2, not_16_out);
  and and_13 (and_13_out, I_2, not_17_out);
  and and_14 (and_14_out, not_18_out, I_1);
  and and_15 (and_15_out, I_2, not_19_out);
  and and_16 (and_16_out, I_2, not_20_out);
  or or_4 (a, and_1_out, I_1, and_2_out, I_3);
  or or_5 (d, and_5_out, and_6_out, and_7_out, and_8_out, I_3);
  or or_6 (f, and_11_out, and_12_out, and_13_out, I_3);
  or or_7 (g, and_14_out, and_15_out, and_16_out, I_3);

  assign p = 1'b0;
endmodule

module transition_logic (
  input  B_1,
  input  B_0,
  input  DS_9,
  input  DS_8,
  input  DS_7,
  input  DS_6,
  input  DS_5,
  input  DS_4,
  input  DS_3,
  input  DS_2,
  input  DS_1,
  input  DS_0,
  input  f
);
endmodule
